# Fritzing sketch breadboard (saved by Fritzing 0.9.3b)
breadboards: 1

parts:
  Part1 = Arduino Uno (Rev3)
  LCD1 = LCD screen
  R1 = Resistor [tolerance=±5% resistance=220 package="1206 [SMD]"]
  BAT1 = BC9VPC [package=bc9vpc]

nets:
  N1: Part1.D11_PWM/MOSI, LCD1.E
  N2: Part1.D12/MISO, LCD1.RS
  N3: Part1.D2, LCD1.DB7
  N4: Part1.D3_PWM, LCD1.DB6
  N5: Part1.D4, LCD1.DB5
  N6: Part1.D5_PWM, LCD1.DB4
  5V: Part1.5V, LCD1.VDD, LCD1.LED+
  GND: Part1.GND, LCD1.VSS, LCD1.R/W, LCD1.LED-, R1.Pin_0, BAT1.V-
  N7: Part1.VIN, BAT1.V+
  N8: LCD1.V0, R1.Pin_1
